# Fritzing sketch wiring (saved by Fritzing 0.9.2b)
breadboards: 1

parts:
  Part1 = Arduino Uno (Rev3)
  IC1 = H-Bridge [package=THT]
  M1 = DC Motor

nets:
  N1: Part1.D10_PWM/SS, IC1.1A
  N2: Part1.D11_PWM/MOSI, IC1.1_2EN
  N3: Part1.D6_PWM, IC1.2A
  N4: Part1.5V, IC1.VCC1
  GND: Part1.GND, IC1.GND1, IC1.GND2, IC1.GND3, IC1.GND4
  N5: Part1.VIN, IC1.VCC2
  N6: IC1.1Y, M1.pin_1
  N7: IC1.2Y, M1.pin_2
